# Fritzing sketch USBChessClock (saved by Fritzing 0.9.2b)

parts:
  Part1 = Arduino Uno (Rev3)
  U1 = LCD-16X2 [package=lcd-16x2]
  Player1_LED = smd LED [color="Red (633nm)" package="0805 [SMD]"]
  Player2_LED = smd LED [color="Red (633nm)" package="0805 [SMD]"]
  J1 = Piezo Speaker
  R3 = Resistor [tolerance=±5% resistance=100 package=THT]  # not connected
  R4 = Resistor [tolerance=±5% resistance=100 package=THT]  # not connected
  S4 = Pushbutton [package="[THT]"]
  J2 = shrouded pin header, 10 pins [form="♂ (shrouded male)"]
  S5 = Toggle Switch [package=THT]
  LCD_3_3k = Resistor [tolerance=±5% resistance=3.3k package=THT]

nets:
  N1: Part1.A5/SCL, S4.Pin_3, S4.Pin_4
  N2: Part1.D8, S5.L1
  N3: Part1.D9_PWM, Player1_LED.cathode
  N4: Part1.D10_PWM/SS, Player2_LED.cathode
  N5: Part1.D11_PWM/MOSI, U1.E
  N6: Part1.D12/MISO, U1.RS
  N7: Part1.GND, J2.pin6
  N8: Part1.D2, U1.DB7
  N9: Part1.D3_PWM, U1.DB6
  N10: Part1.D4, U1.DB5
  N11: Part1.D5_PWM, U1.DB4
  N12: Part1.D6_PWM, J1.pin2
  5V: Part1.5V, U1.VDD, U1.A
  N13: U1.VSS, J2.pin1
  N14: U1.VO, LCD_3_3k.Pin_1
  N15: U1.R_W, J2.pin2
  N16: U1.K, J2.pin10
  N17: Player1_LED.anode, J2.pin8
  N18: Player2_LED.anode, J2.pin9
  N19: J1.pin1, J2.pin4
  N20: S4.Pin_2, J2.pin5
  N21: J2.pin3, LCD_3_3k.Pin_0
  N22: J2.pin7, S5.L2
