# Fritzing sketch USBChessClock (saved by Fritzing 0.9.0b)

parts:
  Part1 = Arduino Uno (Rev3)
  S1 = Toggle Switch [package=THT]
  S2 = Pushbutton [package="[SMD]"]
  U1 = LCD-16X2 [package=lcd-16x2]
  LED1 = smd LED [color="Red (633nm)" package="0805 [SMD]"]
  LED2 = smd LED [color="Red (633nm)" package="0805 [SMD]"]
  R1 = TRIMPOT [package=3386u]
  J1 = Piezo Speaker
  R2 = Resistor [tolerance=±5% resistance=100 package="0805 [SMD]"]
  R3 = Resistor [tolerance=±5% resistance=10k package=THT]

nets:
  N1: Part1.D9_PWM, LED1.cathode
  N2: Part1.D10_PWM/SS, LED2.cathode
  N3: Part1.D11_PWM/MOSI, U1.E
  N4: Part1.D12/MISO, U1.RS
  N5: Part1.D13/SCK, S1.L1
  GND: Part1.GND, U1.VSS, LED1.anode, LED2.anode, J1.pin1, R2.Pin_0, R3.Pin_1
  N6: Part1.D2, U1.DB7
  N7: Part1.D3_PWM, U1.DB6
  N8: Part1.D4, U1.DB5
  N9: Part1.D5_PWM, U1.DB4
  N10: Part1.D6_PWM, J1.pin2
  5V: Part1.D7, Part1.5V, S1.L2, S2.Pin_3, S2.Pin_4, U1.VDD, U1.A, R1.CW
  N11: S2.Pin_1, S2.Pin_2, R3.Pin_0
  N12: U1.VO, R1.WIPER
  N13: U1.K, R2.Pin_1
